// Logisim project SEGMENTOS.circ as structural Verilog: 1 circuit, main circuit main
module main (
  input  A,
  input  B,
  input  C,
  input  D
);

  wire a_out, and_1_out, and_2_out, and_3_out, and_4_out, and_5_out, and_6_out, and_7_out, and_8_out,
       and_9_out, and_10_out, and_11_out, and_12_out, and_13_out, and_14_out, and_15_out, and_16_out,
       and_17_out, and_18_out, and_19_out, and_20_out, and_21_out, and_22_out, and_23_out, and_24_out,
       and_25_out, and_26_out, and_27_out, and_28_out, b_out, c_out, d_out, e_out, f_out, g_out, not_1_out,
       not_2_out, not_3_out, not_4_out, or_1_out, or_2_out, or_3_out, or_4_out, or_5_out, or_6_out, or_7_out,
       or_8_out, or_9_out, or_10_out, or_11_out, xor_1_out;

  not not_1 (not_1_out, A);
  not not_2 (not_2_out, B);
  not not_3 (not_3_out, C);
  not not_4 (not_4_out, D);
  or or_1 (or_1_out, not_1_out, not_4_out, B);
  or or_2 (or_2_out, not_2_out, not_4_out);
  and and_1 (and_1_out, A, not_3_out, D);
  and and_2 (and_2_out, not_2_out, not_4_out);
  and and_3 (and_3_out, not_3_out, not_4_out);
  and and_4 (and_4_out, C, D);
  or or_3 (or_3_out, B, D, not_3_out);
  xor xor_1 (xor_1_out, C, B);
  and and_5 (and_5_out, not_1_out, not_2_out);
  and and_6 (and_6_out, B, C);
  and and_7 (and_7_out, A, not_3_out);
  or or_4 (or_4_out, not_2_out, C);
  or or_5 (or_5_out, B, C);
  and and_8 (and_8_out, or_1_out, C);
  and and_9 (and_9_out, or_2_out, A);
  and and_10 (and_10_out, and_9_out, not_3_out);
  and and_11 (and_11_out, not_1_out, B, D);
  and and_12 (and_12_out, not_4_out, not_2_out);
  or or_6 (or_6_out, and_3_out, and_4_out, not_2_out);
  and and_13 (and_13_out, or_6_out, not_1_out);
  and and_14 (and_14_out, or_3_out, not_1_out);
  and and_15 (and_15_out, A, not_2_out);
  and and_16 (and_16_out, not_3_out, D);
  and and_17 (and_17_out, xor_1_out, D);
  or or_7 (or_7_out, and_5_out, and_6_out, and_7_out);
  and and_18 (and_18_out, or_7_out, not_4_out);
  and and_19 (and_19_out, or_4_out, not_4_out);
  and and_20 (and_20_out, or_5_out, A);
  or u_a (a_out, and_8_out, and_10_out, and_11_out, and_12_out);
  or u_b (b_out, and_1_out, and_2_out, and_13_out);
  or u_c (c_out, and_14_out, and_15_out, and_16_out);
  or u_d (d_out, and_17_out, and_18_out);
  or e (e_out, and_19_out, and_20_out);
  _7_Segment_Display u_7_segment_display_1 (
    .g(g_out), .f(f_out), .a(a_out), .b(b_out), .e(e_out), .d(d_out), .c(c_out));  // open: dp
  and and_21 (and_21_out, or_8_out, A);
  or f (f_out, and_21_out, and_22_out, and_23_out);
  and and_22 (and_22_out, or_9_out, B);
  and and_23 (and_23_out, not_3_out, not_4_out);
  or g (g_out, and_26_out, and_27_out, and_28_out);
  or or_8 (or_8_out, not_2_out, C);
  and and_24 (and_24_out, C, not_4_out);
  or or_9 (or_9_out, and_24_out, and_25_out);
  and and_25 (and_25_out, not_1_out, not_3_out);
  or or_10 (or_10_out, C, D, not_2_out);
  and and_26 (and_26_out, or_10_out, A);
  or or_11 (or_11_out, not_4_out, not_2_out);
  and and_27 (and_27_out, or_11_out, C);
  and and_28 (and_28_out, not_1_out, B, not_3_out);

  // Notes on the sheet:
  //   D
  //   ¬D
  //   ¬C
  //   ¬B
  //   C
  //   ¬A
  //   B
  //   A
endmodule
