// Logisim project cicuitoRelogioDigital.circ as structural Verilog: 14 circuits, main circuit RELOGIO DIGITAL
// DAWD
module RELOGIO_DIGITAL (
  input  in_1,
  input  in_2,
  input  in_3,
  input  in_4,
  input  in_5,
  input  in_6,
  input  in_7,
  input  in_8,
  input  in_9,
  input  in_10,
  input  in_11,
  input  in_12,
  input  in_13,
  input  in_14,
  input  in_15,
  input  in_16,
  input  ON___1,
  input  PM___1
);

  wire AM_PM, am_pm_1__0, am_pm_conversor_1_out_3, ativador_1_out_8, ativador_1_out_9, ativador_1_out_10,
       ativador_1_out_11, ativador_2_out_8, ativador_2_out_9, ativador_2_out_10, ativador_2_out_11,
       ativador_2_out_12, ativador_2_out_13, ativador_3_out_8, ativador_3_out_9, ativador_3_out_10,
       ativador_3_out_11, ativador_3_out_12, ativador_3_out_13, display_am_pm_1_a, display_am_pm_1_a_2,
       display_am_pm_1_b_2, display_am_pm_1_b_3, display_am_pm_1_c, display_am_pm_1_c_2, display_am_pm_1_d,
       display_am_pm_1_d_2, display_am_pm_1_e, display_am_pm_1_e_2, display_am_pm_1_f, display_am_pm_1_f_2,
       display_am_pm_1_g, display_am_pm_1_g_2, horas_1__0, horas_1__1, horas_1__2, horas_1__3, minutos_1__0,
       minutos_1__1, minutos_1__2, minutos_1__3, minutos_1__4, minutos_1__5, minutos_1_nsegundos, P,
       segundos_1__0, segundos_1__1, segundos_1__2, segundos_1__3, segundos_1__4, segundos_1__5,
       segundos_1_nmin;
  wire [7:0] conversor_de_bits_1_saida_dezena, conversor_de_bits_1_saida_unidade,
       conversor_de_bits_2_saida_dezena, conversor_de_bits_2_saida_unidade, conversor_de_bits_3_saida_dezena,
       conversor_de_bits_3_saida_unidade;

  CONVERSOR_DE_BITS conversor_de_bits_1 (
    .A7(1'b0), .A6(1'b0), .A5(1'b0), .A4(1'b0), .A3(horas_1__3), .A2(horas_1__2), .A1(horas_1__1),
    .A0(horas_1__0), .saida_dezena(conversor_de_bits_1_saida_dezena),
    .saida_unidade(conversor_de_bits_1_saida_unidade));
  _7_Segment_Display u_7_segment_display_1 (
    .g(conversor_de_bits_1_saida_dezena[6]), .f(conversor_de_bits_1_saida_dezena[5]),
    .a(conversor_de_bits_1_saida_dezena[4]), .b(conversor_de_bits_1_saida_dezena[3]),
    .e(conversor_de_bits_1_saida_dezena[0]), .d(conversor_de_bits_1_saida_dezena[1]),
    .c(conversor_de_bits_1_saida_dezena[2]));  // open: dp
  ATIVADOR ativador_1 (
    .PAUSE(P), .in_1(1'b0), .in_2(1'b0), .in_3(in_1), .in_4(in_2), .in_5(in_3), .in_6(in_4),
    .out_8(ativador_1_out_8), .out_9(ativador_1_out_9), .out_10(ativador_1_out_10), .out_11(ativador_1_out_11));  // open: out_12, out_13
  HORAS horas_1 (
    .CLOCK(minutos_1_nsegundos), ._3(horas_1__3), ._2(horas_1__2), ._1(horas_1__1), ._0(horas_1__0),
    .AM_PM(AM_PM), .PAUSE(P), .E0(ativador_1_out_8), .E1(ativador_1_out_9), .E2(ativador_1_out_10),
    .E3(ativador_1_out_11));
  _7_Segment_Display u_7_segment_display_2 (
    .g(conversor_de_bits_1_saida_unidade[6]), .f(conversor_de_bits_1_saida_unidade[5]),
    .a(conversor_de_bits_1_saida_unidade[4]), .b(conversor_de_bits_1_saida_unidade[3]),
    .e(conversor_de_bits_1_saida_unidade[0]), .d(conversor_de_bits_1_saida_unidade[1]),
    .c(conversor_de_bits_1_saida_unidade[2]));  // open: dp
  CONVERSOR_DE_BITS conversor_de_bits_2 (
    .A7(1'b0), .A6(1'b0), .A5(minutos_1__5), .A4(minutos_1__4), .A3(minutos_1__3), .A2(minutos_1__2),
    .A1(minutos_1__1), .A0(minutos_1__0), .saida_dezena(conversor_de_bits_2_saida_dezena),
    .saida_unidade(conversor_de_bits_2_saida_unidade));
  _7_Segment_Display u_7_segment_display_3 (
    .g(conversor_de_bits_2_saida_dezena[6]), .f(conversor_de_bits_2_saida_dezena[5]),
    .a(conversor_de_bits_2_saida_dezena[4]), .b(conversor_de_bits_2_saida_dezena[3]),
    .e(conversor_de_bits_2_saida_dezena[0]), .d(conversor_de_bits_2_saida_dezena[1]),
    .c(conversor_de_bits_2_saida_dezena[2]));  // open: dp
  LED led_1 ();  // open: in
  LED led_2 ();  // open: in
  MINUTOS minutos_1 (
    .clock(segundos_1_nmin), ._5(minutos_1__5), ._4(minutos_1__4), ._3(minutos_1__3), ._2(minutos_1__2),
    ._1(minutos_1__1), ._0(minutos_1__0), .nSEGUNDOS(minutos_1_nsegundos), .in_1(ativador_2_out_8),
    .in_2(ativador_2_out_9), .in_4(ativador_2_out_11), .in_5(ativador_2_out_12), .in_3(ativador_2_out_10),
    .in_6(ativador_2_out_13), .in_8(P));
  _7_Segment_Display u_7_segment_display_4 (
    .g(conversor_de_bits_2_saida_unidade[6]), .f(conversor_de_bits_2_saida_unidade[5]),
    .a(conversor_de_bits_2_saida_unidade[4]), .b(conversor_de_bits_2_saida_unidade[3]),
    .e(conversor_de_bits_2_saida_unidade[0]), .d(conversor_de_bits_2_saida_unidade[1]),
    .c(conversor_de_bits_2_saida_unidade[2]));  // open: dp
  ATIVADOR ativador_2 (
    .PAUSE(P), .in_1(in_5), .in_2(in_6), .in_3(in_7), .in_4(in_8), .in_5(in_9), .in_6(in_10),
    .out_8(ativador_2_out_8), .out_9(ativador_2_out_9), .out_10(ativador_2_out_10),
    .out_11(ativador_2_out_11), .out_12(ativador_2_out_12), .out_13(ativador_2_out_13));
  SEGUNDOS segundos_1 (
    .nMIN(segundos_1_nmin), ._5(segundos_1__5), ._4(segundos_1__4), ._3(segundos_1__3), ._2(segundos_1__2),
    ._1(segundos_1__1), ._0(segundos_1__0), .in_1(ativador_3_out_8), .in_2(ativador_3_out_9),
    .in_4(ativador_3_out_11), .in_5(ativador_3_out_12), .in_3(ativador_3_out_10), .in_6(ativador_3_out_13),
    .in_7(P));
  CONVERSOR_DE_BITS conversor_de_bits_3 (
    .A7(1'b0), .A6(1'b0), .A5(segundos_1__5), .A4(segundos_1__4), .A3(segundos_1__3), .A2(segundos_1__2),
    .A1(segundos_1__1), .A0(segundos_1__0), .saida_dezena(conversor_de_bits_3_saida_dezena),
    .saida_unidade(conversor_de_bits_3_saida_unidade));
  _7_Segment_Display u_7_segment_display_5 (
    .g(conversor_de_bits_3_saida_dezena[6]), .f(conversor_de_bits_3_saida_dezena[5]),
    .a(conversor_de_bits_3_saida_dezena[4]), .b(conversor_de_bits_3_saida_dezena[3]),
    .e(conversor_de_bits_3_saida_dezena[0]), .d(conversor_de_bits_3_saida_dezena[1]),
    .c(conversor_de_bits_3_saida_dezena[2]));  // open: dp
  LED led_3 ();  // open: in
  LED led_4 ();  // open: in
  _7_Segment_Display u_7_segment_display_6 (
    .g(conversor_de_bits_3_saida_unidade[6]), .f(conversor_de_bits_3_saida_unidade[5]),
    .a(conversor_de_bits_3_saida_unidade[4]), .b(conversor_de_bits_3_saida_unidade[3]),
    .e(conversor_de_bits_3_saida_unidade[0]), .d(conversor_de_bits_3_saida_unidade[1]),
    .c(conversor_de_bits_3_saida_unidade[2]));  // open: dp
  ATIVADOR ativador_3 (
    .PAUSE(P), .in_1(in_11), .in_2(in_12), .in_3(in_13), .in_4(in_14), .in_5(in_15), .in_6(in_16),
    .out_8(ativador_3_out_8), .out_9(ativador_3_out_9), .out_10(ativador_3_out_10),
    .out_11(ativador_3_out_11), .out_12(ativador_3_out_12), .out_13(ativador_3_out_13));
  not not_1 (P, ON___1);
  AM_PM am_pm_1 (.CLOCK(AM_PM), .E1(am_pm_conversor_1_out_3), ._0(am_pm_1__0), .PAUSE(P));  // open: nAM_PM
  DISPLAY_AM_PM display_am_pm_1 (
    .B(am_pm_1__0), .g(display_am_pm_1_g), .f(display_am_pm_1_f), .a(display_am_pm_1_a),
    .b_2(display_am_pm_1_b_2), .c(display_am_pm_1_c), .e(display_am_pm_1_e), .g_2(display_am_pm_1_g_2),
    .f_2(display_am_pm_1_f_2), .a_2(display_am_pm_1_a_2), .b_3(display_am_pm_1_b_3),
    .c_2(display_am_pm_1_c_2), .d_2(display_am_pm_1_d_2), .e_2(display_am_pm_1_e_2), .d(display_am_pm_1_d));
  _7_Segment_Display u_7_segment_display_7 (
    .g(display_am_pm_1_g), .f(display_am_pm_1_f), .a(display_am_pm_1_a), .b(display_am_pm_1_b_2),
    .e(display_am_pm_1_e), .d(display_am_pm_1_d), .c(display_am_pm_1_c));  // open: dp
  AM_PM_CONVERSOR am_pm_conversor_1 (.in_1(PM___1), .out_3(am_pm_conversor_1_out_3), .in_2(P));
  _7_Segment_Display u_7_segment_display_8 (
    .g(display_am_pm_1_g_2), .f(display_am_pm_1_f_2), .a(display_am_pm_1_a_2), .b(display_am_pm_1_b_3),
    .e(display_am_pm_1_e_2), .d(display_am_pm_1_d_2), .c(display_am_pm_1_c_2));  // open: dp

  // Notes on the sheet:
  //   RELOGIO DIGITAL
  //   ALUNOS
  //   JESSÉ PIRES BARBATO ROCHA
  //   JHONATAN GUILHERME DE OLIVEIRA CUNHA
  //   OFF  (0)
  //   AM  (0)
endmodule

// DISPLAY
module CONVERSOR_DE_BITS (
  input  A7,
  input  A6,
  input  A5,
  input  A4,
  input  A3,
  input  A2,
  input  A1,
  input  A0,
  output [7:0] saida_dezena,
  output [7:0] saida_unidade
);

  wire [7:0] divider_1_rem, divider_2_out, divider_2_rem;

  Divider divider_1 (.a({A7, A6, A5, A4, A3, A2, A1, A0}), .b(8'h64), .rem(divider_1_rem));  // open: out, upper
  Divider divider_2 (.a(divider_1_rem), .b(8'ha), .out(divider_2_out), .rem(divider_2_rem));  // open: upper
  DISPLAY_7_SEGMENTOS display_7_segmentos_1 (
    .A(divider_2_out[3]), .B(divider_2_out[2]), .C(divider_2_out[1]), .D(divider_2_out[0]),
    .g(saida_dezena[6]), .f(saida_dezena[5]), .a_2(saida_dezena[4]), .b_2(saida_dezena[3]),
    .c_2(saida_dezena[2]), .d_2(saida_dezena[1]), .e(saida_dezena[0]));
  DISPLAY_7_SEGMENTOS display_7_segmentos_2 (
    .A(divider_2_rem[3]), .B(divider_2_rem[2]), .C(divider_2_rem[1]), .D(divider_2_rem[0]),
    .g(saida_unidade[6]), .f(saida_unidade[5]), .a_2(saida_unidade[4]), .b_2(saida_unidade[3]),
    .c_2(saida_unidade[2]), .d_2(saida_unidade[1]), .e(saida_unidade[0]));
endmodule

module DISPLAY_7_SEGMENTOS (
  input  A,
  input  B,
  input  C,
  input  D,
  output g,
  output f,
  output a_2,
  output b_2,
  output c_2,
  output d_2,
  output e
);

  wire and_1_out, and_2_out, and_3_out, and_5_out, and_6_out, and_7_out, and_8_out, not_1_out, not_2_out,
       not_3_out, not_4_out, or_3_out, or_6_out, or_7_out, or_9_out, xnor_1_out, xnor_2_out;

  not not_1 (not_1_out, A);
  not not_2 (not_2_out, B);
  not not_3 (not_3_out, C);
  not not_4 (not_4_out, D);
  xnor xnor_1 (xnor_1_out, B, D);
  or or_1 (a_2, xnor_1_out, C, A);
  xnor xnor_2 (xnor_2_out, C, D);
  or or_2 (b_2, xnor_2_out, not_2_out);
  or or_3 (or_3_out, not_4_out, C);
  or or_4 (c_2, B, not_3_out, D);
  and and_1 (and_1_out, C, not_4_out);
  and and_2 (and_2_out, or_3_out, not_2_out);
  or or_5 (d_2, and_2_out, and_1_out, and_3_out, A);
  or or_6 (or_6_out, not_2_out, C);
  and and_3 (and_3_out, B, not_3_out, D);
  and and_4 (e, or_6_out, not_4_out);
  or or_7 (or_7_out, not_3_out, not_4_out);
  and and_5 (and_5_out, or_7_out, B);
  and and_6 (and_6_out, not_3_out, not_4_out);
  or or_8 (f, and_5_out, A, and_6_out);
  or or_9 (or_9_out, not_4_out, not_3_out);
  and and_7 (and_7_out, or_9_out, B);
  or or_10 (g, and_7_out, A, and_8_out);
  and and_8 (and_8_out, not_2_out, C);
endmodule

// FF SEG
module SEGUNDOS (
  input  in_1,
  input  in_2,
  input  in_3,
  input  in_4,
  input  in_5,
  input  in_6,
  input  in_7,
  output nMIN,
  output _5,
  output _4,
  output _3,
  output _2,
  output _1,
  output _0
);

  wire clock_out, j_k_ff_1_qn, j_k_ff_2_qn, j_k_ff_3_qn, j_k_ff_4_qn, j_k_ff_5_qn, not_1_out, or_1_out;

  not not_1 (not_1_out, clock_out);
  Clock clock (.out(clock_out));
  J_K_Flip_Flop j_k_ff_1 (
    .J(1'b1), .clk(not_1_out), .K(1'b1), .Q(_0), .Qn(j_k_ff_1_qn), .preset(in_1), .reset(or_1_out));  // open: en
  J_K_Flip_Flop j_k_ff_2 (
    .J(1'b1), .clk(j_k_ff_1_qn), .K(1'b1), .Q(_1), .Qn(j_k_ff_2_qn), .preset(in_2), .reset(or_1_out));  // open: en
  J_K_Flip_Flop j_k_ff_3 (
    .J(1'b1), .clk(j_k_ff_2_qn), .K(1'b1), .Q(_2), .Qn(j_k_ff_3_qn), .preset(in_3), .reset(or_1_out));  // open: en
  J_K_Flip_Flop j_k_ff_4 (
    .J(1'b1), .clk(j_k_ff_3_qn), .K(1'b1), .Q(_3), .Qn(j_k_ff_4_qn), .preset(in_4), .reset(or_1_out));  // open: en
  J_K_Flip_Flop j_k_ff_5 (
    .J(1'b1), .clk(j_k_ff_4_qn), .K(1'b1), .Q(_4), .Qn(j_k_ff_5_qn), .preset(in_5), .reset(or_1_out));  // open: en
  J_K_Flip_Flop j_k_ff_6 (
    .J(1'b1), .clk(j_k_ff_5_qn), .K(1'b1), .Q(_5), .preset(in_6), .reset(or_1_out));  // open: Qn, en
  or or_1 (or_1_out, nMIN, in_7);
  and and_1 (nMIN, _5, _4, _3, _2);
endmodule

// FF MIN
module MINUTOS (
  input  in_1,
  input  in_2,
  input  in_3,
  input  in_4,
  input  in_5,
  input  in_6,
  input  clock,
  input  in_8,
  output nSEGUNDOS,
  output _5,
  output _4,
  output _3,
  output _2,
  output _1,
  output _0
);

  wire j_k_ff_1_qn, j_k_ff_2_qn, j_k_ff_3_qn, j_k_ff_4_qn, j_k_ff_5_qn, not_1_out, or_1_out;

  not not_1 (not_1_out, clock);
  J_K_Flip_Flop j_k_ff_1 (
    .J(1'b1), .clk(not_1_out), .K(1'b1), .Q(_0), .Qn(j_k_ff_1_qn), .preset(in_1), .reset(or_1_out));  // open: en
  J_K_Flip_Flop j_k_ff_2 (
    .J(1'b1), .clk(j_k_ff_1_qn), .K(1'b1), .Q(_1), .Qn(j_k_ff_2_qn), .preset(in_2), .reset(or_1_out));  // open: en
  J_K_Flip_Flop j_k_ff_3 (
    .J(1'b1), .clk(j_k_ff_2_qn), .K(1'b1), .Q(_2), .Qn(j_k_ff_3_qn), .preset(in_3), .reset(or_1_out));  // open: en
  J_K_Flip_Flop j_k_ff_4 (
    .J(1'b1), .clk(j_k_ff_3_qn), .K(1'b1), .Q(_3), .Qn(j_k_ff_4_qn), .preset(in_4), .reset(or_1_out));  // open: en
  J_K_Flip_Flop j_k_ff_5 (
    .J(1'b1), .clk(j_k_ff_4_qn), .K(1'b1), .Q(_4), .Qn(j_k_ff_5_qn), .preset(in_5), .reset(or_1_out));  // open: en
  J_K_Flip_Flop j_k_ff_6 (
    .J(1'b1), .clk(j_k_ff_5_qn), .K(1'b1), .Q(_5), .preset(in_6), .reset(or_1_out));  // open: Qn, en
  or or_1 (or_1_out, nSEGUNDOS, in_8);
  and and_1 (nSEGUNDOS, _5, _4, _3, _2);
endmodule

// FF HRS
module HORAS (
  input  E0,
  input  E1,
  input  E2,
  input  E3,
  input  CLOCK,
  input  PAUSE,
  output AM_PM,
  output _3,
  output _2,
  output _1,
  output _0
);

  wire _1_t, _2_t, _3_t, _4, _5, _6, and_2_out, auxiliar2_clear_hora_1_clear, j_k_ff_1_qn, j_k_ff_2_qn,
       j_k_ff_3_qn, not_1_out, or_1_out, or_2_out;

  not not_1 (not_1_out, CLOCK);
  or or_1 (or_1_out, PAUSE, E0);
  J_K_Flip_Flop j_k_ff_1 (
    .J(1'b1), .clk(not_1_out), .K(1'b1), .Q(_0), .Qn(j_k_ff_1_qn), .preset(or_1_out),
    .reset(auxiliar2_clear_hora_1_clear));  // open: en
  AUXILIAR2_CLEAR_HORA auxiliar2_clear_hora_1 (
    .in_2(_2_t), .in_3(_3_t), .in_4(_4), .in_5(_5), .in_6(_6), .clear(auxiliar2_clear_hora_1_clear),
    .in_1(_1_t));
  J_K_Flip_Flop j_k_ff_2 (
    .J(1'b1), .clk(j_k_ff_1_qn), .K(1'b1), .Q(_1), .Qn(j_k_ff_2_qn), .preset(E1), .reset(or_2_out));  // open: en
  and and_1 (AM_PM, _2, _3);
  J_K_Flip_Flop j_k_ff_3 (
    .J(1'b1), .clk(j_k_ff_2_qn), .K(1'b1), .Q(_2), .Qn(j_k_ff_3_qn), .preset(E2), .reset(or_2_out));  // open: en
  AUXILIAR_CLEAR_HORA auxiliar_clear_hora_1 (
    .out_5(_1_t), .out_6(_2_t), .out_7(_3_t), .out_8(_4), .out_9(_5), .out_10(_6), .E0(E0), .E1(E1), .E2(E2),
    .E3(E3));
  J_K_Flip_Flop j_k_ff_4 (
    .J(1'b1), .clk(j_k_ff_3_qn), .K(1'b1), .Q(_3), .preset(E3), .reset(or_2_out));  // open: Qn, en
  or or_2 (or_2_out, and_2_out, PAUSE);
  and and_2 (and_2_out, _3, _2, _0);
endmodule

// CONVERSOR
module ATIVADOR (
  input  in_1,
  input  in_2,
  input  in_3,
  input  in_4,
  input  in_5,
  input  in_6,
  input  PAUSE,
  output out_8,
  output out_9,
  output out_10,
  output out_11,
  output out_12,
  output out_13
);

  and and_1 (out_13, PAUSE, in_1);
  and and_2 (out_11, PAUSE, in_3);
  and and_3 (out_12, PAUSE, in_2);
  and and_4 (out_9, PAUSE, in_5);
  and and_5 (out_10, PAUSE, in_4);
  and and_6 (out_8, PAUSE, in_6);
endmodule

module AM_PM_CONVERSOR (
  input  in_1,
  input  in_2,
  output out_3
);

  and and_1 (out_3, in_1, in_2);
endmodule

// FF
module AM_PM (
  input  E1,
  input  CLOCK,
  input  PAUSE,
  output nAM_PM,
  output _0
);

  wire j_k_ff_1_qn, j_k_ff_2_q, not_1_out, or_1_out;

  not not_1 (not_1_out, CLOCK);
  J_K_Flip_Flop j_k_ff_1 (
    .J(1'b1), .clk(not_1_out), .K(1'b1), .Q(_0), .Qn(j_k_ff_1_qn), .preset(E1));  // open: en, reset
  J_K_Flip_Flop j_k_ff_2 (
    .J(1'b1), .clk(j_k_ff_1_qn), .K(1'b1), .Q(j_k_ff_2_q), .reset(or_1_out));  // open: Qn, preset, en
  or or_1 (or_1_out, nAM_PM, PAUSE);
  and and_1 (nAM_PM, j_k_ff_2_q, _0);
endmodule

// DISPLAY AM/PM
module DISPLAY_AM_PM (
  input  B,
  output g,
  output f,
  output a,
  output b_2,
  output c,
  output d,
  output e,
  output g_2,
  output f_2,
  output a_2,
  output b_3,
  output c_2,
  output d_2,
  output e_2
);

  not not_1 (c, B);

  assign a = 1'b1;
  assign a_2 = 1'b1;
  assign b_2 = 1'b1;
  assign b_3 = 1'b0;
  assign c_2 = 1'b1;
  assign d = 1'b0;
  assign d_2 = 1'b0;
  assign e = 1'b1;
  assign e_2 = 1'b1;
  assign f = 1'b1;
  assign f_2 = 1'b0;
  assign g = 1'b1;
  assign g_2 = 1'b1;

  // Notes on the sheet:
  //   A OU P
  //   M
endmodule

module CONVERSOR_HORAS (
  input  in_1,
  input  in_2,
  input  in_3,
  input  in_4,
  input  PAUSE,
  output out_6,
  output out_7,
  output out_8,
  output out_9
);

  wire and_1_out, and_2_out, not_1_out;

  and and_1 (and_1_out, not_1_out, in_1);
  and and_2 (and_2_out, not_1_out, in_2);
  and and_3 (out_7, not_1_out, in_3);
  and and_4 (out_6, not_1_out, in_4);
  xor xor_1 (out_9, and_2_out, not_1_out);
  xor xor_2 (out_8, and_1_out, not_1_out);
  not not_1 (not_1_out, PAUSE);
endmodule

module ATIVADOR_HORAS (
  input  in_1,
  input  in_2,
  input  in_3,
  input  in_4,
  input  in_5,
  input  in_6,
  input  PAUSE,
  output out_8,
  output out_9,
  output out_10,
  output out_11,
  output out_12,
  output out_13
);

  wire and_6_out, nor_1_out;

  and and_1 (out_13, PAUSE, in_1);
  or or_1 (out_8, nor_1_out, and_6_out);
  and and_2 (out_11, PAUSE, in_3);
  and and_3 (out_12, PAUSE, in_2);
  and and_4 (out_10, PAUSE, in_4);
  and and_5 (out_9, PAUSE, in_5);
  and and_6 (and_6_out, PAUSE, in_6);
  nor nor_1 (nor_1_out, in_1, in_2, in_3, PAUSE, in_4, in_5, in_6);
endmodule

module AUXILIAR_CLEAR_HORA (
  input  E0,
  input  E1,
  input  E2,
  input  E3,
  output out_5,
  output out_6,
  output out_7,
  output out_8,
  output out_9,
  output out_10
);

  wire not_1_out, not_2_out, not_3_out, not_4_out, not_5_out, not_6_out, not_7_out, not_8_out, not_9_out,
       not_10_out, not_11_out, not_12_out, not_13_out, not_14_out, not_15_out;

  not not_1 (not_1_out, E0);
  not not_2 (not_2_out, E0);
  not not_3 (not_3_out, E0);
  not not_4 (not_4_out, E0);
  not not_5 (not_5_out, E0);
  not not_6 (not_6_out, E0);
  not not_7 (not_7_out, E3);
  not not_8 (not_8_out, E2);
  and and_1 (out_5, E3, not_8_out, not_9_out, not_1_out);
  not not_9 (not_9_out, E1);
  not not_10 (not_10_out, E3);
  and and_2 (out_6, not_10_out, E2, not_11_out, not_2_out);
  not not_11 (not_11_out, E1);
  not not_12 (not_12_out, E2);
  and and_3 (out_7, E1, not_12_out, not_13_out, not_3_out);
  not not_13 (not_13_out, E3);
  and and_4 (out_8, E3, E2, not_14_out, not_4_out);
  not not_14 (not_14_out, E1);
  and and_5 (out_9, not_7_out, E2, E1, not_5_out);
  not not_15 (not_15_out, E2);
  and and_6 (out_10, E3, not_15_out, E1, not_6_out);
endmodule

module AUXILIAR2_CLEAR_HORA (
  input  in_1,
  input  in_2,
  input  in_3,
  input  in_4,
  input  in_5,
  input  in_6,
  output clear
);

  or or_1 (clear, in_1, in_2, in_3, in_4, in_5, in_6);
endmodule
